// Logisim project circuits.circ as structural Verilog: 2 circuits, main circuit main
module main (
  input  A,
  input  B,
  input  C,
  output X
);

  wire and_1_out, and_2_out;

  and and_1 (and_1_out, A, B);
  and and_2 (and_2_out, B, C);
  or or_1 (X, and_1_out, and_2_out);
endmodule

module two (
  input  A,
  input  B,
  output X
);

  wire and_1_out, not_1_out;

  and and_1 (and_1_out, A, B);
  not not_1 (not_1_out, B);
  and and_2 (X, and_1_out, not_1_out);
endmodule
