// Logisim project and-output-type-nor-circuit.circ as structural Verilog: 2 circuits, main circuit main
module main (
);

  wire nor_1_out, nor_2_out, nor_3_out, nor_4_out, nor_5_out, nor_6_out, undriven, undriven_2, undriven_3;

  nor nor_1 (nor_1_out, undriven, undriven);
  nor nor_2 (nor_2_out, undriven_2, undriven_2);
  nor nor_3 (nor_3_out, undriven_3, undriven_3);
  nor nor_4 (nor_4_out, nor_1_out, nor_2_out);
  nor nor_5 (nor_5_out, nor_4_out, nor_4_out);
  nor nor_6 (nor_6_out, nor_5_out, nor_3_out);

  // Notes on the sheet:
  //   A
  //   B
  //   C
  //   X
endmodule

module simulate (
  input  A,
  input  B,
  input  C,
  output X
);

  wire nor_1_out, nor_2_out, nor_3_out, nor_4_out, nor_5_out;

  nor nor_1 (nor_1_out, A, A);
  nor nor_2 (nor_2_out, B, B);
  nor nor_3 (nor_3_out, C, C);
  nor nor_4 (nor_4_out, nor_1_out, nor_2_out);
  nor nor_5 (nor_5_out, nor_4_out, nor_4_out);
  nor nor_6 (X, nor_5_out, nor_3_out);
endmodule
