// Logisim project or-output-type-nor-circuit.circ as structural Verilog: 1 circuit, main circuit OR
module OR (
  input  A,
  input  B,
  output X
);

  wire nor_1_out;

  nor nor_1 (nor_1_out, A, B);
  nor nor_2 (X, nor_1_out, nor_1_out);
endmodule
