// Logisim project q29-resultant-circuit.circ as structural Verilog: 1 circuit, main circuit q29-resultant-circuit
module q29_resultant_circuit (
  input  A,
  input  B,
  input  C,
  output X
);

  wire nor_1_out, nor_2_out, nor_3_out, nor_4_out, nor_5_out, nor_6_out, nor_7_out, nor_8_out, nor_9_out,
       nor_10_out, nor_11_out, nor_12_out, nor_13_out, nor_14_out, nor_15_out, nor_16_out, nor_17_out,
       nor_18_out, nor_19_out, nor_21_out, nor_22_out, undriven, undriven_2, undriven_3;

  nor nor_1 (nor_1_out, A, A);
  nor nor_2 (nor_2_out, B, B);
  nor nor_3 (nor_3_out, nor_1_out, nor_2_out);
  nor nor_4 (nor_4_out, undriven, undriven);
  nor nor_5 (nor_5_out, undriven_2, undriven_2);
  nor nor_6 (nor_6_out, nor_4_out, nor_5_out);
  nor nor_7 (nor_7_out, nor_3_out, nor_3_out);
  nor nor_8 (nor_8_out, nor_6_out, nor_6_out);
  nor nor_9 (nor_9_out, nor_7_out, nor_7_out);
  nor nor_10 (nor_10_out, nor_8_out, nor_8_out);
  nor nor_11 (nor_11_out, nor_9_out, nor_9_out);
  nor nor_12 (nor_12_out, B, B);
  nor nor_13 (nor_13_out, C, C);
  nor nor_14 (nor_14_out, nor_11_out, nor_12_out);
  nor nor_15 (nor_15_out, nor_10_out, nor_10_out);
  nor nor_16 (nor_16_out, undriven_2, undriven_2);
  nor nor_17 (nor_17_out, undriven_3, undriven_3);
  nor nor_18 (nor_18_out, nor_14_out, nor_14_out);
  nor nor_19 (nor_19_out, nor_15_out, nor_16_out);
  nor nor_20 (X, nor_18_out, nor_13_out);
  nor nor_21 (nor_21_out, nor_19_out, nor_19_out);
  nor nor_22 (nor_22_out, nor_21_out, nor_17_out);

  // Notes on the sheet:
  //   A
  //   B
  //   C
  //   X
endmodule
