// Logisim project q3-33-question-circuit.circ as structural Verilog: 13 circuits, main circuit Photo
module Photo (
);

  wire and_1_out, and_2_out, and_3_out, not_1_out, not_2_out, or_1_out, undriven, undriven_2, undriven_3,
       undriven_4, undriven_5;

  not not_1 (not_1_out, undriven_2);
  not not_2 (not_2_out, undriven_3);
  and and_1 (and_1_out, undriven, not_1_out);
  and and_2 (and_2_out, not_1_out, not_2_out, undriven_4);
  and and_3 (and_3_out, undriven_2, not_2_out, undriven_4, undriven_5);
  or or_1 (or_1_out, and_1_out, and_2_out, and_3_out);

  // Notes on the sheet:
  //   B
  //   E
  //   C
  //   A
  //   D
  //   X
endmodule

module Simulation (
  input  B,
  input  E,
  input  C,
  input  A,
  input  D,
  output X
);

  wire and_1_out, and_2_out, and_3_out, not_1_out, not_2_out;

  not not_1 (not_1_out, E);
  not not_2 (not_2_out, C);
  and and_1 (and_1_out, B, not_1_out);
  and and_2 (and_2_out, not_1_out, not_2_out, A);
  and and_3 (and_3_out, E, not_2_out, A, D);
  or or_1 (X, and_1_out, and_2_out, and_3_out);
endmodule

module NAND_as_NOT (
);

  wire nand_1_out, undriven;

  nand nand_1 (nand_1_out, undriven, undriven);

  // Notes on the sheet:
  //   A
  //   X
endmodule

module NAND_as_OR (
);

  wire nand_1_out, nand_2_out, nand_3_out, undriven, undriven_2;

  nand nand_1 (nand_1_out, undriven, undriven);
  nand nand_2 (nand_2_out, undriven_2, undriven_2);
  nand nand_3 (nand_3_out, nand_1_out, nand_2_out);

  // Notes on the sheet:
  //   A
  //   B
  //   X
endmodule

module NAND_as_3OR (
);

  wire nand_1_out, nand_2_out, nand_3_out, nand_4_out, undriven, undriven_2, undriven_3;

  nand nand_1 (nand_1_out, undriven, undriven);
  nand nand_2 (nand_2_out, undriven_2, undriven_2);
  nand nand_3 (nand_3_out, undriven_3, undriven_3);
  nand nand_4 (nand_4_out, nand_1_out, nand_2_out, nand_3_out);

  // Notes on the sheet:
  //   A
  //   B
  //   C
  //   X
endmodule

module NAND_as_3OR_Simulation (
  input  A,
  input  B,
  input  C,
  output X
);

  wire nand_1_out, nand_2_out, nand_3_out;

  nand nand_1 (nand_1_out, A, A);
  nand nand_2 (nand_2_out, B, B);
  nand nand_3 (nand_3_out, C, C);
  nand nand_4 (X, nand_1_out, nand_2_out, nand_3_out);
endmodule

module NAND_as_2AND (
);

  wire nand_1_out, nand_2_out, undriven, undriven_2;

  nand nand_1 (nand_1_out, undriven, undriven_2);
  nand nand_2 (nand_2_out, nand_1_out, nand_1_out);

  // Notes on the sheet:
  //   A
  //   B
  //   X
endmodule

module _3NAND_as_3AND (
);

  wire nand_1_out, nand_2_out, undriven, undriven_2, undriven_3;

  nand nand_1 (nand_1_out, undriven, undriven_2, undriven_3);
  nand nand_2 (nand_2_out, nand_1_out, nand_1_out, nand_1_out);

  // Notes on the sheet:
  //   A
  //   B
  //   C
  //   X
endmodule

module NAND_as_3AND_Simulation (
  input  A,
  input  B,
  input  C,
  output X
);

  wire nand_1_out;

  nand nand_1 (nand_1_out, A, B, C);
  nand nand_2 (X, nand_1_out, nand_1_out, nand_1_out);
endmodule

module _4NAND_as_4AND (
);

  wire nand_1_out, nand_2_out, undriven, undriven_2, undriven_3, undriven_4;

  nand nand_1 (nand_1_out, undriven, undriven_2, undriven_3, undriven_4);
  nand nand_2 (nand_2_out, nand_1_out, nand_1_out, nand_1_out, nand_1_out);

  // Notes on the sheet:
  //   A
  //   B
  //   C
  //   D
  //   X
endmodule

module _4NAND_as_4AND_Simulation (
  input  A,
  input  B,
  input  C,
  input  D,
  output X
);

  wire nand_1_out;

  nand nand_1 (nand_1_out, A, B, C, D);
  nand nand_2 (X, nand_1_out, nand_1_out, nand_1_out, nand_1_out);
endmodule

module NAND_Photo_Simulation (
  input  B,
  input  E,
  input  C,
  input  A,
  input  D,
  output X
);

  wire nand_1_out, nand_2_out, nand_3_out, nand_4_out, nand_5_out, nand_6_out, nand_7_out, nand_8_out,
       nand_9_out, nand_10_out, nand_11_out, nand_12_out, nand_13_out, nand_14_out, nand_15_out, nand_16_out,
       nand_17_out, nand_18_out, nand_19_out, nand_20_out, nand_21_out, nand_22_out, undriven, undriven_2,
       undriven_3, undriven_4, undriven_5, undriven_6, undriven_7, undriven_8, undriven_9, undriven_10,
       undriven_11, undriven_12, undriven_13;

  nand nand_1 (nand_1_out, undriven, undriven);
  nand nand_2 (nand_2_out, undriven_2, undriven_2);
  nand nand_3 (nand_3_out, undriven_3, undriven_3);
  nand nand_4 (nand_4_out, undriven_4, undriven_5);
  nand nand_5 (nand_5_out, undriven_6, undriven_7, undriven_8);
  nand nand_6 (nand_6_out, undriven_13, undriven_13);
  nand nand_7 (nand_7_out, nand_4_out, nand_4_out);
  nand nand_8 (nand_8_out, undriven_9, undriven_10, undriven_11, undriven_12);
  nand nand_9 (nand_9_out, nand_1_out, nand_2_out, nand_3_out);
  nand nand_10 (nand_10_out, nand_5_out, nand_5_out, nand_5_out);
  nand nand_11 (nand_11_out, nand_8_out, nand_8_out, nand_8_out, nand_8_out);
  nand nand_12 (nand_12_out, E, E);
  nand nand_13 (nand_13_out, C, C);
  nand nand_14 (nand_14_out, B, nand_12_out);
  nand nand_15 (nand_15_out, nand_12_out, nand_13_out, A);
  nand nand_16 (nand_16_out, E, nand_13_out, A, D);
  nand nand_17 (nand_17_out, nand_14_out, nand_14_out);
  nand nand_18 (nand_18_out, nand_15_out, nand_15_out, nand_15_out);
  nand nand_19 (nand_19_out, nand_16_out, nand_16_out, nand_16_out, nand_16_out);
  nand nand_20 (nand_20_out, nand_17_out, nand_17_out);
  nand nand_21 (nand_21_out, nand_18_out, nand_18_out);
  nand nand_22 (nand_22_out, nand_19_out, nand_19_out);
  nand nand_23 (X, nand_20_out, nand_21_out, nand_22_out);
endmodule

module NAND_Photo (
);

  wire nand_1_out, nand_2_out, nand_3_out, nand_4_out, nand_5_out, nand_6_out, nand_7_out, nand_8_out,
       nand_9_out, nand_10_out, nand_11_out, nand_12_out, undriven, undriven_2, undriven_3, undriven_4,
       undriven_5;

  nand nand_1 (nand_1_out, undriven_2, undriven_2);
  nand nand_2 (nand_2_out, undriven_3, undriven_3);
  nand nand_3 (nand_3_out, undriven, nand_1_out);
  nand nand_4 (nand_4_out, nand_1_out, nand_2_out, undriven_4);
  nand nand_5 (nand_5_out, undriven_2, nand_2_out, undriven_4, undriven_5);
  nand nand_6 (nand_6_out, nand_3_out, nand_3_out);
  nand nand_7 (nand_7_out, nand_4_out, nand_4_out, nand_4_out);
  nand nand_8 (nand_8_out, nand_5_out, nand_5_out, nand_5_out, nand_5_out);
  nand nand_9 (nand_9_out, nand_6_out, nand_6_out);
  nand nand_10 (nand_10_out, nand_7_out, nand_7_out);
  nand nand_11 (nand_11_out, nand_8_out, nand_8_out);
  nand nand_12 (nand_12_out, nand_9_out, nand_10_out, nand_11_out);

  // Notes on the sheet:
  //   B
  //   E
  //   C
  //   A
  //   D
  //   X
endmodule
